// Logisim project lab5.circ as structural Verilog: 7 circuits, main circuit main
module main (
  input  Reset,
  input  [2:0] Sel,
  output Probe1_s_0,
  output Probe1_s_1,
  output Probe1_s_2,
  output Probe1_s_3
);

  wire clk_out;

  Clock #(.highDuration(4), .lowDuration(4)) clk (.out(clk_out));
  Clock sysclk ();  // open: out
  // Probe on {Probe1_s_3, Probe1_s_2, Probe1_s_1, Probe1_s_0}
  Universal universal_1 (
    .clk(clk_out), .rst(Reset), .Sel(Sel), .COut({Probe1_s_3, Probe1_s_2, Probe1_s_1, Probe1_s_0}));
  Hex_Digit_Display hex_digit_display_1 (.value({Probe1_s_3, Probe1_s_2, Probe1_s_1, Probe1_s_0}));  // open: dp

  // Notes on the sheet:
  //   Yerulan Kongrat
  //   Lab 5: Counters
endmodule

module A_Up (
  input  clk,
  input  rst,
  output [3:0] Up
);

  wire d_ff_1_qn, d_ff_2_qn, d_ff_3_qn, d_ff_4_qn;

  D_Flip_Flop d_ff_1 (.D(d_ff_1_qn), .clk(clk), .Q(Up[0]), .Qn(d_ff_1_qn), .reset(rst));  // open: preset
  D_Flip_Flop d_ff_2 (.D(d_ff_2_qn), .clk(d_ff_1_qn), .Q(Up[1]), .Qn(d_ff_2_qn), .reset(rst));  // open: preset
  D_Flip_Flop d_ff_3 (.D(d_ff_3_qn), .clk(d_ff_2_qn), .Q(Up[2]), .Qn(d_ff_3_qn), .reset(rst));  // open: preset
  D_Flip_Flop d_ff_4 (.D(d_ff_4_qn), .clk(d_ff_3_qn), .Q(Up[3]), .Qn(d_ff_4_qn), .reset(rst));  // open: preset
endmodule

module A_Down (
  input  clk,
  input  rst,
  output [3:0] Down
);

  wire d_ff_1_qn, d_ff_2_qn, d_ff_3_qn, d_ff_4_qn;

  D_Flip_Flop d_ff_1 (.D(d_ff_1_qn), .clk(clk), .Q(Down[0]), .Qn(d_ff_1_qn), .preset(rst));  // open: reset
  D_Flip_Flop d_ff_2 (.D(d_ff_2_qn), .clk(Down[0]), .Q(Down[1]), .Qn(d_ff_2_qn), .preset(rst));  // open: reset
  D_Flip_Flop d_ff_3 (.D(d_ff_3_qn), .clk(Down[1]), .Q(Down[2]), .Qn(d_ff_3_qn), .preset(rst));  // open: reset
  D_Flip_Flop d_ff_4 (.D(d_ff_4_qn), .clk(Down[2]), .Q(Down[3]), .Qn(d_ff_4_qn), .preset(rst));  // open: reset
endmodule

module A_Decade (
  input  clk,
  input  rst,
  output [3:0] Decade
);

  wire and_1_out, d_ff_1_qn, d_ff_2_qn, d_ff_3_qn, d_ff_4_qn, or_1_out;

  D_Flip_Flop d_ff_1 (.D(d_ff_1_qn), .clk(clk), .Q(Decade[0]), .Qn(d_ff_1_qn), .reset(or_1_out));  // open: preset
  or or_1 (or_1_out, rst, and_1_out);
  D_Flip_Flop d_ff_2 (.D(d_ff_2_qn), .clk(d_ff_1_qn), .Q(Decade[1]), .Qn(d_ff_2_qn), .reset(or_1_out));  // open: preset
  D_Flip_Flop d_ff_3 (.D(d_ff_3_qn), .clk(d_ff_2_qn), .Q(Decade[2]), .Qn(d_ff_3_qn), .reset(or_1_out));  // open: preset
  D_Flip_Flop d_ff_4 (.D(d_ff_4_qn), .clk(d_ff_3_qn), .Q(Decade[3]), .Qn(d_ff_4_qn), .reset(or_1_out));  // open: preset
  and and_1 (and_1_out, Decade[3], Decade[1]);
endmodule

module S_Ring (
  input  clk,
  input  rst,
  output [3:0] Ring
);

  D_Flip_Flop d_ff_1 (.D(Ring[3]), .clk(clk), .Q(Ring[0]), .preset(rst));  // open: Qn, reset
  D_Flip_Flop d_ff_2 (.D(Ring[0]), .clk(clk), .Q(Ring[1]), .reset(rst));  // open: Qn, preset
  D_Flip_Flop d_ff_3 (.D(Ring[1]), .clk(clk), .Q(Ring[2]), .reset(rst));  // open: Qn, preset
  D_Flip_Flop d_ff_4 (.D(Ring[2]), .clk(clk), .Q(Ring[3]), .reset(rst));  // open: Qn, preset
endmodule

module S_Johnson (
  input  clk,
  input  rst,
  output [3:0] Johnson
);

  wire d_ff_4_qn;

  D_Flip_Flop d_ff_1 (.D(d_ff_4_qn), .clk(clk), .Q(Johnson[0]), .preset(rst));  // open: Qn, reset
  D_Flip_Flop d_ff_2 (.D(Johnson[0]), .clk(clk), .Q(Johnson[1]), .reset(rst));  // open: Qn, preset
  D_Flip_Flop d_ff_3 (.D(Johnson[1]), .clk(clk), .Q(Johnson[2]), .reset(rst));  // open: Qn, preset
  D_Flip_Flop d_ff_4 (.D(Johnson[2]), .clk(clk), .Q(Johnson[3]), .Qn(d_ff_4_qn), .reset(rst));  // open: preset
endmodule

module Universal (
  input  clk,
  input  rst,
  input  [2:0] Sel,
  output [3:0] COut
);

  wire [3:0] a_decade_1_decade, a_down_1_down, a_up_1_up, s_johnson_1_johnson, s_ring_1_ring;

  A_Up a_up_1 (.clk(clk), .rst(rst), .Up(a_up_1_up));
  A_Down a_down_1 (.clk(clk), .rst(rst), .Down(a_down_1_down));
  A_Decade a_decade_1 (.clk(clk), .rst(rst), .Decade(a_decade_1_decade));
  S_Ring s_ring_1 (.clk(clk), .rst(rst), .Ring(s_ring_1_ring));
  S_Johnson s_johnson_1 (.clk(clk), .rst(rst), .Johnson(s_johnson_1_johnson));
  Multiplexer #(.select(3), .width(4)) multiplexer_1 (
    .in0(a_up_1_up), .in1(a_down_1_down), .in2(a_decade_1_decade), .in3(s_ring_1_ring),
    .in4(s_johnson_1_johnson), .in5(s_johnson_1_johnson), .in6(s_johnson_1_johnson),
    .in7(s_johnson_1_johnson), .out(COut), .sel(Sel));
endmodule
